# Fritzing sketch Master_slave_setup (saved by Fritzing 0.9.10b)
breadboards: 1

parts:
  Mod1 = Amica NodeMCU DEVKIT 1.0
  Part1 = Arduino Uno (Rev3)

nets:
  N1: Mod1.pin1, Mod1.pin_10, Mod1.pin_26
  N2: Mod1.pin2, Mod1.pin_9, Mod1.pin_25, Mod1.pin_29, Part1.GND
  N3: Mod1.pin_11, Part1.A5/SCL
  N4: Mod1.pin_12, Part1.A4/SDA
